# Fritzing sketch Fritzing Base (saved by Fritzing 0.9.3b)
circuit board: 5.1cm x 2.3cm

parts:
  Bluefruit = Adafruit Feather M0 Bluefruit LE [part_number="Adafruit #2995"]
  Socket = shrouded pin header, 12 pins [form="♂ (shrouded male)"]

nets:
  N1: Bluefruit.A2, Socket.pin12
  N2: Bluefruit.A1, Socket.pin11
  N3: Bluefruit.A0, Socket.pin10
  N4: Bluefruit.GND, Socket.pin9
  N5: Bluefruit.D13, Socket.pin8
  N6: Bluefruit.D12, Socket.pin7
  N7: Bluefruit.D11, Socket.pin6
  N8: Bluefruit.D10, Socket.pin5
  N9: Bluefruit.D6, Socket.pin4
  N10: Bluefruit.D5, Socket.pin3
  N11: Bluefruit.SCL, Socket.pin2
  N12: Bluefruit.SDA, Socket.pin1

custom parts:
  Adafruit Feather M0 Bluefruit LE: This is the Adafruit Feather M0 Bluefruit LE - our take on an 'all-in-one' Arduino-compatible + Bluetooth Low Energy with built in USB and battery charging. Its an Adafruit Feather M0 with a BTLE module, ready to rock! We have other boards in the Feather family, check'em out here. Bluetooth Low Energy is the hottest new low-power, 2.4GHz spectrum wireless protocol. In particular, its the only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
