# Fritzing sketch Fritzing Baseb (saved by Fritzing 0.9.3b)
circuit board: 5.1cm x 2.3cm

parts:
  Bluefruit = Adafruit Feather M0 Bluefruit LE [part_number="Adafruit #2995"]
  Socket = shrouded pin header, 16 pins [form="♂ (shrouded male)"]
  S1 = Toggle Switch [package=THT]
  S2 = Toggle Switch [package=THT]
  S4 = Toggle Switch [package=THT]
  S3 = Toggle Switch [package=THT]
  S5 = Pushbutton [package="[THT]"]
  LED1 = LED - 5mm [color="Red (633nm)" package="5 mm [THT]"]
  LED2 = LED - 5mm [color="Green (555nm)" package="5 mm [THT]"]
  J2 = female pin header, 8 pins [form="♀ (female)"]
  J1 = female pin header, 8 pins [form="♀ (female)"]

nets:
  N1: Bluefruit.A2, Socket.pin12
  N2: Bluefruit.A1, Socket.pin11
  N3: Bluefruit.A0, Socket.pin10
  N4: Bluefruit.GND, Socket.pin9
  N5: Bluefruit.D13, Socket.pin8
  N6: Bluefruit.D12, Socket.pin7
  N7: Bluefruit.D11, Socket.pin6
  N8: Bluefruit.D10, Socket.pin5
  N9: Bluefruit.D6, Socket.pin4
  N10: Bluefruit.D5, Socket.pin3
  N11: Bluefruit.SCL, Socket.pin2
  N12: Bluefruit.SDA, Socket.pin1
  N13: S1.L1, J2.pin4
  N14: S1.COM, S2.COM, S4.COM, S3.COM, S5.Pin_4, LED1.cathode, LED2.cathode, J1.pin1
  N15: S1.L2, J1.pin4
  N16: S2.L1, J2.pin5
  N17: S2.L2, J1.pin3
  N18: S4.L1, J2.pin7
  N19: S4.L2, J2.pin8
  N20: S3.L1, J2.pin6
  N21: S3.L2, J1.pin2
  N22: S5.Pin_1, S5.Pin_2, J2.pin3
  N23: LED1.anode, J2.pin2
  N24: LED2.anode, J2.pin1

custom parts:
  Adafruit Feather M0 Bluefruit LE: This is the Adafruit Feather M0 Bluefruit LE - our take on an 'all-in-one' Arduino-compatible + Bluetooth Low Energy with built in USB and battery charging. Its an Adafruit Feather M0 with a BTLE module, ready to rock! We have other boards in the Feather family, check'em out here. Bluetooth Low Energy is the hottest new low-power, 2.4GHz spectrum wireless protocol. In particular, its the only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
